// Logisim project ICS233_PROJECT.circ as structural Verilog: 7 circuits, main circuit Register_File
module Register_File (
  input  [15:0] BusW,
  input  [2:0] Rs1,
  input  [2:0] RD,
  input  [2:0] Rs2,
  input  RegWrite,
  input  Cllock,
  output [15:0] BusA,
  output [15:0] BusB
);

  wire and_1_out, and_2_out, and_3_out, and_4_out, and_5_out, and_6_out, and_7_out, and_8_out,
       decoder_1_out0, decoder_1_out1, decoder_1_out2, decoder_1_out3, decoder_1_out4, decoder_1_out5,
       decoder_1_out6, decoder_1_out7;
  wire [15:0] register_1_q, register_2_q, register_3_q, register_4_q, register_5_q, register_6_q,
       register_7_q, register_8_q;

  Decoder #(.select(3), .enable("false")) decoder_1 (
    .out0(decoder_1_out0), .out1(decoder_1_out1), .out2(decoder_1_out2), .out3(decoder_1_out3),
    .out4(decoder_1_out4), .out5(decoder_1_out5), .out6(decoder_1_out6), .out7(decoder_1_out7), .sel(RD));
  and and_1 (and_1_out, decoder_1_out0, RegWrite);
  and and_2 (and_2_out, decoder_1_out1, RegWrite);
  and and_3 (and_3_out, decoder_1_out2, RegWrite);
  and and_4 (and_4_out, decoder_1_out3, RegWrite);
  and and_5 (and_5_out, decoder_1_out4, RegWrite);
  and and_6 (and_6_out, decoder_1_out5, RegWrite);
  and and_7 (and_7_out, decoder_1_out6, RegWrite);
  and and_8 (and_8_out, decoder_1_out7, RegWrite);
  Register #(.width(16)) register_1 (.D(BusW), .en(and_1_out), .Q(register_1_q), .clk(Cllock), .clr(1'b0));
  Register #(.width(16)) register_2 (.D(BusW), .en(and_2_out), .Q(register_2_q), .clk(Cllock), .clr(1'b0));
  Register #(.width(16)) register_3 (.D(BusW), .en(and_3_out), .Q(register_3_q), .clk(Cllock), .clr(1'b0));
  Register #(.width(16)) register_4 (.D(BusW), .en(and_4_out), .Q(register_4_q), .clk(Cllock), .clr(1'b0));
  Register #(.width(16)) register_5 (.D(BusW), .en(and_5_out), .Q(register_5_q), .clk(Cllock), .clr(1'b0));
  Register #(.width(16)) register_6 (.D(BusW), .en(and_6_out), .Q(register_6_q), .clk(Cllock), .clr(1'b0));
  Register #(.width(16)) register_7 (.D(BusW), .en(and_7_out), .Q(register_7_q), .clk(Cllock), .clr(1'b0));
  Register #(.width(16)) register_8 (.D(BusW), .en(and_8_out), .Q(register_8_q), .clk(Cllock), .clr(1'b0));
  Multiplexer #(.select(3), .width(16)) multiplexer_1 (
    .in0(register_1_q), .in1(register_2_q), .in2(register_3_q), .in3(register_4_q), .in4(register_5_q),
    .in5(register_6_q), .in6(register_7_q), .out(BusA), .sel(Rs1));  // open: in7, en
  Multiplexer #(.select(3), .width(16)) multiplexer_2 (
    .in0(register_1_q), .in1(register_2_q), .in2(register_3_q), .in3(register_4_q), .in4(register_5_q),
    .in5(register_6_q), .in6(register_7_q), .in7(register_8_q), .out(BusB), .sel(Rs2));  // open: en
endmodule

module Logic_Gate (
  input  [15:0] in_1,
  input  [15:0] in_2,
  input  [1:0] F,
  output [15:0] \output 
);

  wire [15:0] and_1_out, or_1_out, xor_1_out;

  assign and_1_out = in_1 & in_2;  // AND_Gate and_1, 16 bits wide
  assign or_1_out = in_1 | in_2;  // OR_Gate or_1, 16 bits wide
  assign xor_1_out = in_1 ^ in_2;  // XOR_Gate xor_1, 16 bits wide
  Multiplexer #(.select(2), .width(16)) multiplexer_1 (
    .in0(xor_1_out), .in1(or_1_out), .in2(and_1_out), .out(\output ), .sel(F));  // open: in3, en

  // Notes on the sheet:
  //   A
  //   B
endmodule

module Arithematic (
  input  [15:0] in_1,
  input  [15:0] in_2,
  input  [1:0] F,
  output [15:0] Output
);

  wire comparator_1_lt, comparator_2_lt;
  wire [15:0] adder_1_out, bit_extender_1_out, bit_extender_2_out, bit_extender_3_out, xor_1_out;

  assign bit_extender_1_out = {{15{F[0]}}, F[0]};  // Bit_Extender bit_extender_1
  assign xor_1_out = in_2 ^ bit_extender_1_out;  // XOR_Gate xor_1, 16 bits wide
  Adder #(.width(16)) adder_1 (.a(in_1), .b(xor_1_out), .out(adder_1_out));  // open: cin, cout
  Comparator #(.width(16)) comparator_1 (.a(in_1), .b(in_2), .lt(comparator_1_lt));  // open: gt, eq
  Comparator #(.width(16), .mode("unsigned")) comparator_2 (.a(in_1), .b(in_2), .lt(comparator_2_lt));  // open: gt, eq
  assign bit_extender_2_out = {{15{1'b0}}, comparator_1_lt};  // Bit_Extender bit_extender_2
  assign bit_extender_3_out = {{15{1'b0}}, comparator_2_lt};  // Bit_Extender bit_extender_3
  Multiplexer #(.select(2), .width(16)) multiplexer_1 (
    .in0(adder_1_out), .in1(adder_1_out), .in2(bit_extender_2_out), .in3(bit_extender_3_out), .out(Output),
    .sel(F));  // open: en

  // Notes on the sheet:
  //   A
  //   B
endmodule

module Shifter (
  input  [15:0] in_1,
  input  [15:0] in_2,
  input  [1:0] F,
  output [15:0] Output
);

  wire [3:0] bit_extender_1_out;
  wire [15:0] shifter_1_out, shifter_2_out, shifter_3_out;

  Bit_Extender #(.in_width(16), .out_width(4)) bit_extender_1 (.in(in_2), .out(bit_extender_1_out));
  Shifter_part #(.width(16)) shifter_1 (.in(in_1), .\dist (bit_extender_1_out), .out(shifter_1_out));
  Shifter_part #(.width(16), .shift("lr")) shifter_2 (.in(in_1), .\dist (bit_extender_1_out), .out(shifter_2_out));
  Shifter_part #(.width(16), .shift("ar")) shifter_3 (.in(in_1), .\dist (bit_extender_1_out), .out(shifter_3_out));
  Multiplexer #(.select(2), .width(16)) multiplexer_1 (
    .in0(shifter_1_out), .in1(shifter_2_out), .in2(shifter_3_out), .out(Output), .sel(F));  // open: in3, en

  // Notes on the sheet:
  //   A
  //   B
endmodule

module CPU (
  input  [2:0] in_1
);

  wire and_1_out, clock_1_out, or_1_out;
  wire [15:0] adder_1_out, bit_extender_1_out, bit_extender_2_out, bit_extender_3_out, multiplexer_1_out,
       register_1_q, rom_1_data;

  Clock clock_1 (.out(clock_1_out));
  assign bit_extender_1_out = {{13{1'b0}}, in_1};  // Bit_Extender bit_extender_1
  Register #(.width(16)) register_1 (.D(adder_1_out), .Q(register_1_q), .clk(clock_1_out));  // open: en, clr
  Adder #(.width(16)) adder_1 (.a(bit_extender_1_out), .b(register_1_q), .out(adder_1_out));  // open: cin, cout
  RAM #(.addrWidth(16), .dataWidth(16), .bus("separate")) ram_1 ();  // open: addr, din, data, str, sel, clk, ld, clr
  ROM #(.addrWidth(16), .dataWidth(16)) rom_1 (.addr(register_1_q), .data(rom_1_data));  // open: sel
  assign bit_extender_2_out = {{11{rom_1_data[15]}}, rom_1_data[15:11]};  // Bit_Extender bit_extender_2
  assign bit_extender_3_out = {{11{1'b0}}, rom_1_data[15:11]};  // Bit_Extender bit_extender_3
  and and_1 (and_1_out, rom_1_data[1], rom_1_data[2]);
  Multiplexer #(.width(16)) multiplexer_1 (
    .in0(bit_extender_2_out), .in1(bit_extender_3_out), .out(multiplexer_1_out), .sel(or_1_out));  // open: en
  or or_1 (or_1_out, and_1_out, rom_1_data[3]);
endmodule

module ALU (
  input  [15:0] in_1,
  input  [15:0] in_2,
  input  [1:0] F,
  input  [1:0] OP,
  output [15:0] Output
);

  wire [15:0] arithematic_1_output, logic_gate_1_output, shifter_1_output;

  Shifter shifter_1 (.in_1(in_1), .in_2(in_2), .F(F), .Output(shifter_1_output));
  Arithematic arithematic_1 (.in_1(in_1), .in_2(in_2), .F(F), .Output(arithematic_1_output));
  Logic_Gate logic_gate_1 (.in_1(in_1), .in_2(in_2), .F(F), .\output (logic_gate_1_output));
  Multiplexer #(.select(2), .width(16)) multiplexer_1 (
    .in0(shifter_1_output), .in1(arithematic_1_output), .in2(logic_gate_1_output), .out(Output), .sel(OP));  // open: in3, en

  // Notes on the sheet:
  //   A
  //   B
endmodule

module Instruction_Memory (
  input  [4:0] OP,
  input  [2:0] Rd,
  input  [2:0] Rs1,
  input  [15:0] PC,
  input  [2:0] Rs2,
  input  [1:0] f,
  input  [10:0] imm11,
  input  [4:0] imm2u_imm3l,
  input  [4:0] imm5
);

  ROM #(.addrWidth(16), .dataWidth(16)) rom_1 (
    .addr(PC), .data({f, imm5[2:0], imm11[5:3], imm2u_imm3l[2:0], OP}));  // open: sel

  assign imm2u_imm3l[4:3] = f;
  assign imm5[4:3] = f;
  assign {imm11[10:6], imm11[2:0]} = {f, imm5[2:0], imm2u_imm3l[2:0]};
  assign Rd = imm2u_imm3l[2:0];
  assign Rs1 = imm11[5:3];
  assign Rs2 = imm5[2:0];
endmodule
